// Logisim project CL.circ as structural Verilog: 5 circuits, main circuit main
module main (
  input  SELECIONA_CONTADOR
);

  wire Contador1dez_adez, Contador1dez_bdez, Contador1dez_cdez, Contador1dez_ddez, Contador1unid_aunid,
       Contador1unid_bunid, Contador1unid_cunid, Contador1unid_dunid, Contador1unid_tc, Contador2dez_adez,
       Contador2dez_bdez, Contador2dez_cdez, Contador2dez_ddez, Contador2unid_aunid, Contador2unid_bunid,
       Contador2unid_cunid, Contador2unid_dunid, Contador2unid_tc, decod_dez_a_2, decod_dez_b_2,
       decod_dez_c_2, decod_dez_d_2, decod_dez_e, decod_dez_f, decod_dez_g, decod_unid_a_2, decod_unid_b_2,
       decod_unid_c_2, decod_unid_d_2, decod_unid_e, decod_unid_f, decod_unid_g, MUX_dezenas_za,
       MUX_dezenas_zb, MUX_dezenas_zc, MUX_dezenas_zd, MUX_unidades_za, MUX_unidades_zb, MUX_unidades_zc,
       MUX_unidades_zd;

  ContadorBCDunid Contador2unid (
    .TC(Contador2unid_tc), .Aunid(Contador2unid_aunid), .Bunid(Contador2unid_bunid),
    .Cunid(Contador2unid_cunid), .Dunid(Contador2unid_dunid));
  ContadorBCDdez Contador2dez (
    .EN(Contador2unid_tc), .Adez(Contador2dez_adez), .Bdez(Contador2dez_bdez), .Cdez(Contador2dez_cdez),
    .Ddez(Contador2dez_ddez));
  ContadorBCDunid Contador1unid (
    .TC(Contador1unid_tc), .Aunid(Contador1unid_aunid), .Bunid(Contador1unid_bunid),
    .Cunid(Contador1unid_cunid), .Dunid(Contador1unid_dunid));
  ContadorBCDdez Contador1dez (
    .EN(Contador1unid_tc), .Adez(Contador1dez_adez), .Bdez(Contador1dez_bdez), .Cdez(Contador1dez_cdez),
    .Ddez(Contador1dez_ddez));
  MUX74ALS157 MUX_dezenas (
    .I1a(Contador1dez_adez), .I0a(Contador2dez_adez), .I1b(Contador1dez_bdez), .I0b(Contador2dez_bdez),
    .I1c(Contador1dez_cdez), .I0c(Contador2dez_cdez), .I1d(Contador1dez_ddez), .I0d(Contador2dez_ddez),
    .in_9(SELECIONA_CONTADOR), .Za(MUX_dezenas_za), .Zb(MUX_dezenas_zb), .Zc(MUX_dezenas_zc),
    .Zd(MUX_dezenas_zd));
  MUX74ALS157 MUX_unidades (
    .I1a(Contador1unid_aunid), .I0a(Contador2unid_aunid), .I1b(Contador1unid_bunid),
    .I0b(Contador2unid_bunid), .I1c(Contador1unid_cunid), .I0c(Contador2unid_cunid),
    .I1d(Contador1unid_dunid), .I0d(Contador2unid_dunid), .in_9(SELECIONA_CONTADOR), .Za(MUX_unidades_za),
    .Zb(MUX_unidades_zb), .Zc(MUX_unidades_zc), .Zd(MUX_unidades_zd));
  Decoder decod_dez (
    .A(MUX_dezenas_za), .B(MUX_dezenas_zb), .C(MUX_dezenas_zc), .D(MUX_dezenas_zd), .a_2(decod_dez_a_2),
    .b_2(decod_dez_b_2), .c_2(decod_dez_c_2), .d_2(decod_dez_d_2), .e(decod_dez_e), .f(decod_dez_f),
    .g(decod_dez_g));
  Decoder decod_unid (
    .A(MUX_unidades_za), .B(MUX_unidades_zb), .C(MUX_unidades_zc), .D(MUX_unidades_zd), .a_2(decod_unid_a_2),
    .b_2(decod_unid_b_2), .c_2(decod_unid_c_2), .d_2(decod_unid_d_2), .e(decod_unid_e), .f(decod_unid_f),
    .g(decod_unid_g));
  _7_Segment_Display u_7_segment_display_1 (
    .g(decod_unid_g), .f(decod_unid_f), .a(decod_unid_a_2), .b(decod_unid_b_2), .e(decod_unid_e),
    .d(decod_unid_d_2), .c(decod_unid_c_2));  // open: dp
  _7_Segment_Display u_7_segment_display_2 (
    .g(decod_dez_g), .f(decod_dez_f), .a(decod_dez_a_2), .b(decod_dez_b_2), .e(decod_dez_e),
    .d(decod_dez_d_2), .c(decod_dez_c_2));  // open: dp
endmodule

module MUX74ALS157 (
  input  I1a,
  input  I0a,
  input  I1b,
  input  I0b,
  input  I1c,
  input  I0c,
  input  I1d,
  input  I0d,
  input  in_9,
  output Za,
  output Zb,
  output Zc,
  output Zd
);

  wire and_1_out, and_2_out, and_3_out, and_4_out, and_5_out, and_6_out, and_7_out, and_8_out, nor_1_out,
       nor_2_out, nor_3_out, nor_4_out, not_1_out, not_2_out, not_3_out;

  not not_1 (not_1_out, in_9);
  not not_2 (not_2_out, not_1_out);
  not not_3 (not_3_out, 1'b0);
  and and_1 (and_1_out, I1a, not_2_out, not_3_out);
  and and_2 (and_2_out, I0a, not_1_out, not_3_out);
  and and_3 (and_3_out, I1b, not_2_out, not_3_out);
  and and_4 (and_4_out, I0b, not_1_out, not_3_out);
  and and_5 (and_5_out, I1c, not_2_out, not_3_out);
  and and_6 (and_6_out, I0c, not_1_out, not_3_out);
  and and_7 (and_7_out, I1d, not_2_out, not_3_out);
  and and_8 (and_8_out, I0d, not_1_out, not_3_out);
  nor nor_1 (nor_1_out, and_1_out, and_2_out);
  nor nor_2 (nor_2_out, and_3_out, and_4_out);
  nor nor_3 (nor_3_out, and_5_out, and_6_out);
  nor nor_4 (nor_4_out, and_7_out, and_8_out);
  not not_4 (Za, nor_1_out);
  not not_5 (Zb, nor_2_out);
  not not_6 (Zc, nor_3_out);
  not not_7 (Zd, nor_4_out);
endmodule

module Decoder (
  input  A,
  input  B,
  input  C,
  input  D,
  output a_2,
  output b_2,
  output c_2,
  output d_2,
  output e,
  output f,
  output g
);

  wire and_1_out, and_2_out, and_3_out, and_4_out, and_6_out, and_7_out, and_8_out, and_9_out, not_1_out,
       not_2_out, not_3_out, not_4_out, not_5_out, not_6_out, not_7_out, not_8_out, not_9_out, not_10_out,
       not_11_out, not_12_out, not_13_out, not_14_out, not_15_out, not_16_out, or_1_out, or_2_out, or_3_out,
       xnor_1_out, xor_1_out;

  not not_1 (not_1_out, C);
  not not_2 (not_2_out, B);
  not not_3 (not_3_out, D);
  not not_4 (not_4_out, C);
  not not_5 (not_5_out, A);
  not not_6 (not_6_out, B);
  not not_7 (not_7_out, D);
  not not_8 (not_8_out, D);
  or or_1 (or_1_out, not_2_out, C);
  not not_9 (not_9_out, C);
  not not_10 (not_10_out, D);
  and and_1 (and_1_out, not_3_out, not_4_out);
  and and_2 (and_2_out, not_5_out, not_6_out, not_7_out);
  not not_11 (not_11_out, B);
  or or_2 (or_2_out, not_9_out, not_10_out);
  and and_3 (and_3_out, B, D);
  not not_12 (not_12_out, B);
  or or_3 (or_3_out, not_11_out, C);
  not not_13 (not_13_out, D);
  and and_4 (and_4_out, B, not_1_out, D);
  and and_5 (e, not_8_out, or_1_out);
  and and_6 (and_6_out, or_2_out, B);
  and and_7 (and_7_out, not_12_out, C);
  and and_8 (and_8_out, or_3_out, not_13_out);
  not not_14 (not_14_out, B);
  xnor xnor_1 (xnor_1_out, C, D);
  not not_15 (not_15_out, C);
  not not_16 (not_16_out, D);
  and and_9 (and_9_out, not_16_out, C);
  xor xor_1 (xor_1_out, C, B);
  or or_4 (a_2, A, C, and_3_out, and_2_out);
  or or_5 (b_2, not_14_out, xnor_1_out);
  or or_6 (c_2, A, B, not_15_out, D);
  or or_7 (d_2, A, and_7_out, and_8_out, and_4_out);
  or or_8 (f, A, and_6_out, and_1_out);
  or or_9 (g, A, and_9_out, xor_1_out);
endmodule

module ContadorBCDunid (
  output Aunid,
  output Bunid,
  output Cunid,
  output Dunid,
  output TC
);

  wire and_1_out, and_2_out, clock_1_out, nand_1_out, nand_2_out, not_1_out, not_3_out, not_4_out, not_5_out;

  Clock clock_1 (.out(clock_1_out));
  J_K_Flip_Flop j_k_ff_1 (.J(1'b1), .clk(clock_1_out), .K(1'b1), .Q(Dunid), .reset(not_1_out));  // open: Qn, preset, en
  not not_1 (not_1_out, nand_1_out);
  not not_2 (TC, nand_2_out);
  J_K_Flip_Flop j_k_ff_2 (
    .J(Dunid), .clk(clock_1_out), .K(Dunid), .Q(Cunid), .reset(not_3_out));  // open: Qn, preset, en
  not not_3 (not_3_out, nand_1_out);
  nand nand_1 (nand_1_out, Cunid, Aunid);
  and and_1 (and_1_out, Dunid, Cunid);
  J_K_Flip_Flop j_k_ff_3 (
    .J(and_1_out), .clk(clock_1_out), .K(and_1_out), .Q(Bunid), .reset(not_4_out));  // open: Qn, preset, en
  not not_4 (not_4_out, nand_1_out);
  and and_2 (and_2_out, Dunid, Cunid, Bunid);
  J_K_Flip_Flop j_k_ff_4 (
    .J(and_2_out), .clk(clock_1_out), .K(and_2_out), .Q(Aunid), .reset(not_5_out));  // open: Qn, preset, en
  not not_5 (not_5_out, nand_1_out);
  nand nand_2 (nand_2_out, Aunid, Dunid);
endmodule

module ContadorBCDdez (
  input  EN,
  output Adez,
  output Bdez,
  output Cdez,
  output Ddez
);

  wire and_1_out, and_2_out, clock_1_out, nand_1_out, not_1_out, not_2_out, not_3_out, not_4_out;

  Clock clock_1 (.out(clock_1_out));
  J_K_Flip_Flop j_k_ff_1 (
    .J(1'b1), .clk(clock_1_out), .K(1'b1), .Q(Ddez), .en(EN), .reset(not_1_out));  // open: Qn, preset
  not not_1 (not_1_out, nand_1_out);
  J_K_Flip_Flop j_k_ff_2 (
    .J(Ddez), .clk(clock_1_out), .K(Ddez), .Q(Cdez), .en(EN), .reset(not_2_out));  // open: Qn, preset
  not not_2 (not_2_out, nand_1_out);
  nand nand_1 (nand_1_out, Cdez, Adez);
  not not_3 (not_3_out, nand_1_out);
  and and_1 (and_1_out, Ddez, Cdez);
  J_K_Flip_Flop j_k_ff_3 (
    .J(and_1_out), .clk(clock_1_out), .K(and_1_out), .Q(Bdez), .en(EN), .reset(not_3_out));  // open: Qn, preset
  and and_2 (and_2_out, Ddez, Cdez, Bdez);
  J_K_Flip_Flop j_k_ff_4 (
    .J(and_2_out), .clk(clock_1_out), .K(and_2_out), .Q(Adez), .en(EN), .reset(not_4_out));  // open: Qn, preset
  not not_4 (not_4_out, nand_1_out);
endmodule
