// Logisim project RelogioDigital.circ as structural Verilog: 9 circuits, main circuit main
module main (
);

  wire contadorbcddezhora_1__2hora, contadorbcddezhora_1_adez, contadorbcddezhora_1_bdez,
       contadorbcddezhora_1_cdez, contadorbcddezhora_1_ddez, contadorbcddezmin_1_adez,
       contadorbcddezmin_1_bdez, contadorbcddezmin_1_cdez, contadorbcddezmin_1_ddez,
       contadorbcddezmin_1_out_6, contadorbcddezseg_1_adez, contadorbcddezseg_1_bdez,
       contadorbcddezseg_1_cdez, contadorbcddezseg_1_ddez, contadorbcddezseg_1_out_6,
       contadorbcdunidmin_1_aunid, contadorbcdunidmin_1_bunid, contadorbcdunidmin_1_cunid,
       contadorbcdunidmin_1_dunid, contadorbcdunidmin_1_tc, contadorbcdunidseg_1_aunid,
       contadorbcdunidseg_1_bunid, contadorbcdunidseg_1_cunid, contadorbcdunidseg_1_dunid,
       contadorbcdunidseg_1_tc, contadorbcdunihora_1_aunid, contadorbcdunihora_1_bunid,
       contadorbcdunihora_1_cunid, contadorbcdunihora_1_dunid, contadorbcdunihora_1_meianoite,
       contadorbcdunihora_1_tc, decoder_1_a_2, decoder_1_b_2, decoder_1_c_2, decoder_1_d_2, decoder_1_e,
       decoder_1_f, decoder_1_g, decoder_2_a_2, decoder_2_b_2, decoder_2_c_2, decoder_2_d_2, decoder_2_e,
       decoder_2_f, decoder_2_g, decoder_3_a_2, decoder_3_b_2, decoder_3_c_2, decoder_3_d_2, decoder_3_e,
       decoder_3_f, decoder_3_g, decoder_4_a_2, decoder_4_b_2, decoder_4_c_2, decoder_4_d_2, decoder_4_e,
       decoder_4_f, decoder_4_g, decoder_5_a_2, decoder_5_b_2, decoder_5_c_2, decoder_5_d_2, decoder_5_e,
       decoder_5_f, decoder_5_g, decoder_6_a_2, decoder_6_b_2, decoder_6_c_2, decoder_6_d_2, decoder_6_e,
       decoder_6_f, decoder_6_g;

  ContadorBCDdezHORA contadorbcddezhora_1 (
    .EN(contadorbcdunihora_1_tc), .Adez(contadorbcddezhora_1_adez), .Bdez(contadorbcddezhora_1_bdez),
    .Cdez(contadorbcddezhora_1_cdez), .Ddez(contadorbcddezhora_1_ddez),
    .meia_noite(contadorbcdunihora_1_meianoite), ._2hora(contadorbcddezhora_1__2hora));
  Decoder decoder_1 (
    .A(contadorbcddezhora_1_adez), .B(contadorbcddezhora_1_bdez), .C(contadorbcddezhora_1_cdez),
    .D(contadorbcddezhora_1_ddez), .a_2(decoder_1_a_2), .b_2(decoder_1_b_2), .c_2(decoder_1_c_2),
    .d_2(decoder_1_d_2), .e(decoder_1_e), .f(decoder_1_f), .g(decoder_1_g));
  ContadorBCDuniHORA contadorbcdunihora_1 (
    .TC(contadorbcdunihora_1_tc), .in_1(contadorbcddezmin_1_out_6),
    .meianoite(contadorbcdunihora_1_meianoite), .Aunid(contadorbcdunihora_1_aunid),
    .Bunid(contadorbcdunihora_1_bunid), .Cunid(contadorbcdunihora_1_cunid),
    .Dunid(contadorbcdunihora_1_dunid), ._2Hora(contadorbcddezhora_1__2hora));
  _7_Segment_Display u_7_segment_display_1 (
    .g(decoder_1_g), .f(decoder_1_f), .a(decoder_1_a_2), .b(decoder_1_b_2), .e(decoder_1_e),
    .d(decoder_1_d_2), .c(decoder_1_c_2));  // open: dp
  Decoder decoder_2 (
    .A(contadorbcdunihora_1_aunid), .B(contadorbcdunihora_1_bunid), .C(contadorbcdunihora_1_cunid),
    .D(contadorbcdunihora_1_dunid), .a_2(decoder_2_a_2), .b_2(decoder_2_b_2), .c_2(decoder_2_c_2),
    .d_2(decoder_2_d_2), .e(decoder_2_e), .f(decoder_2_f), .g(decoder_2_g));
  _7_Segment_Display u_7_segment_display_2 (
    .g(decoder_2_g), .f(decoder_2_f), .a(decoder_2_a_2), .b(decoder_2_b_2), .e(decoder_2_e),
    .d(decoder_2_d_2), .c(decoder_2_c_2));  // open: dp
  ContadorBCDdezMIN contadorbcddezmin_1 (
    .out_6(contadorbcddezmin_1_out_6), .EN(contadorbcdunidmin_1_tc), .Adez(contadorbcddezmin_1_adez),
    .Bdez(contadorbcddezmin_1_bdez), .Cdez(contadorbcddezmin_1_cdez), .Ddez(contadorbcddezmin_1_ddez));
  Decoder decoder_3 (
    .A(contadorbcddezmin_1_adez), .B(contadorbcddezmin_1_bdez), .C(contadorbcddezmin_1_cdez),
    .D(contadorbcddezmin_1_ddez), .a_2(decoder_3_a_2), .b_2(decoder_3_b_2), .c_2(decoder_3_c_2),
    .d_2(decoder_3_d_2), .e(decoder_3_e), .f(decoder_3_f), .g(decoder_3_g));
  ContadorBCDunidMIN contadorbcdunidmin_1 (
    .TC(contadorbcdunidmin_1_tc), .in_1(contadorbcddezseg_1_out_6), .Aunid(contadorbcdunidmin_1_aunid),
    .Bunid(contadorbcdunidmin_1_bunid), .Cunid(contadorbcdunidmin_1_cunid), .Dunid(contadorbcdunidmin_1_dunid));
  _7_Segment_Display u_7_segment_display_3 (
    .g(decoder_3_g), .f(decoder_3_f), .a(decoder_3_a_2), .b(decoder_3_b_2), .e(decoder_3_e),
    .d(decoder_3_d_2), .c(decoder_3_c_2));  // open: dp
  Decoder decoder_4 (
    .A(contadorbcdunidmin_1_aunid), .B(contadorbcdunidmin_1_bunid), .C(contadorbcdunidmin_1_cunid),
    .D(contadorbcdunidmin_1_dunid), .a_2(decoder_4_a_2), .b_2(decoder_4_b_2), .c_2(decoder_4_c_2),
    .d_2(decoder_4_d_2), .e(decoder_4_e), .f(decoder_4_f), .g(decoder_4_g));
  _7_Segment_Display u_7_segment_display_4 (
    .g(decoder_4_g), .f(decoder_4_f), .a(decoder_4_a_2), .b(decoder_4_b_2), .e(decoder_4_e),
    .d(decoder_4_d_2), .c(decoder_4_c_2));  // open: dp
  ContadorBCDdezSEG contadorbcddezseg_1 (
    .out_6(contadorbcddezseg_1_out_6), .EN(contadorbcdunidseg_1_tc), .Adez(contadorbcddezseg_1_adez),
    .Bdez(contadorbcddezseg_1_bdez), .Cdez(contadorbcddezseg_1_cdez), .Ddez(contadorbcddezseg_1_ddez));
  Decoder decoder_5 (
    .A(contadorbcddezseg_1_adez), .B(contadorbcddezseg_1_bdez), .C(contadorbcddezseg_1_cdez),
    .D(contadorbcddezseg_1_ddez), .a_2(decoder_5_a_2), .b_2(decoder_5_b_2), .c_2(decoder_5_c_2),
    .d_2(decoder_5_d_2), .e(decoder_5_e), .f(decoder_5_f), .g(decoder_5_g));
  _7_Segment_Display u_7_segment_display_5 (
    .g(decoder_5_g), .f(decoder_5_f), .a(decoder_5_a_2), .b(decoder_5_b_2), .e(decoder_5_e),
    .d(decoder_5_d_2), .c(decoder_5_c_2));  // open: dp
  _7_Segment_Display u_7_segment_display_6 (
    .g(decoder_6_g), .f(decoder_6_f), .a(decoder_6_a_2), .b(decoder_6_b_2), .e(decoder_6_e),
    .d(decoder_6_d_2), .c(decoder_6_c_2));  // open: dp
  ContadorBCDunidSEG contadorbcdunidseg_1 (
    .TC(contadorbcdunidseg_1_tc), .Aunid(contadorbcdunidseg_1_aunid), .Bunid(contadorbcdunidseg_1_bunid),
    .Cunid(contadorbcdunidseg_1_cunid), .Dunid(contadorbcdunidseg_1_dunid));
  Decoder decoder_6 (
    .A(contadorbcdunidseg_1_aunid), .B(contadorbcdunidseg_1_bunid), .C(contadorbcdunidseg_1_cunid),
    .D(contadorbcdunidseg_1_dunid), .a_2(decoder_6_a_2), .b_2(decoder_6_b_2), .c_2(decoder_6_c_2),
    .d_2(decoder_6_d_2), .e(decoder_6_e), .f(decoder_6_f), .g(decoder_6_g));
endmodule

module ContadorBCDunidSEG (
  output Aunid,
  output Bunid,
  output Cunid,
  output Dunid,
  output TC
);

  wire and_1_out, and_2_out, clock_1_out, nand_1_out, nand_2_out, not_1_out, not_3_out, not_4_out, not_5_out;

  Clock clock_1 (.out(clock_1_out));
  J_K_Flip_Flop j_k_ff_1 (.J(1'b1), .clk(clock_1_out), .K(1'b1), .Q(Dunid), .reset(not_1_out));  // open: Qn, preset, en
  not not_1 (not_1_out, nand_1_out);
  not not_2 (TC, nand_2_out);
  J_K_Flip_Flop j_k_ff_2 (
    .J(Dunid), .clk(clock_1_out), .K(Dunid), .Q(Cunid), .reset(not_3_out));  // open: Qn, preset, en
  not not_3 (not_3_out, nand_1_out);
  nand nand_1 (nand_1_out, Cunid, Aunid);
  and and_1 (and_1_out, Dunid, Cunid);
  J_K_Flip_Flop j_k_ff_3 (
    .J(and_1_out), .clk(clock_1_out), .K(and_1_out), .Q(Bunid), .reset(not_4_out));  // open: Qn, preset, en
  not not_4 (not_4_out, nand_1_out);
  and and_2 (and_2_out, Dunid, Cunid, Bunid);
  J_K_Flip_Flop j_k_ff_4 (
    .J(and_2_out), .clk(clock_1_out), .K(and_2_out), .Q(Aunid), .reset(not_5_out));  // open: Qn, preset, en
  not not_5 (not_5_out, nand_1_out);
  nand nand_2 (nand_2_out, Aunid, Dunid);
endmodule

module ContadorBCDdezSEG (
  input  EN,
  output Adez,
  output Bdez,
  output Cdez,
  output Ddez,
  output out_6
);

  wire and_1_out, and_2_out, clock_1_out, nand_1_out, nand_2_out, not_1_out, not_3_out, not_4_out, not_5_out;

  Clock clock_1 (.out(clock_1_out));
  J_K_Flip_Flop j_k_ff_1 (
    .J(1'b1), .clk(clock_1_out), .K(1'b1), .Q(Ddez), .en(EN), .reset(not_1_out));  // open: Qn, preset
  not not_1 (not_1_out, nand_1_out);
  not not_2 (out_6, nand_2_out);
  J_K_Flip_Flop j_k_ff_2 (
    .J(Ddez), .clk(clock_1_out), .K(Ddez), .Q(Cdez), .en(EN), .reset(not_3_out));  // open: Qn, preset
  not not_3 (not_3_out, nand_1_out);
  nand nand_1 (nand_1_out, Cdez, Bdez);
  not not_4 (not_4_out, nand_1_out);
  and and_1 (and_1_out, Ddez, Cdez);
  J_K_Flip_Flop j_k_ff_3 (
    .J(and_1_out), .clk(clock_1_out), .K(and_1_out), .Q(Bdez), .en(EN), .reset(not_4_out));  // open: Qn, preset
  and and_2 (and_2_out, Ddez, Cdez, Bdez);
  J_K_Flip_Flop j_k_ff_4 (
    .J(and_2_out), .clk(clock_1_out), .K(and_2_out), .Q(Adez), .en(EN), .reset(not_5_out));  // open: Qn, preset
  not not_5 (not_5_out, nand_1_out);
  nand nand_2 (nand_2_out, Bdez, Ddez, EN);
endmodule

module Decoder (
  input  A,
  input  B,
  input  C,
  input  D,
  output a_2,
  output b_2,
  output c_2,
  output d_2,
  output e,
  output f,
  output g
);

  wire and_1_out, and_2_out, and_3_out, and_4_out, and_6_out, and_7_out, and_8_out, and_9_out, not_1_out,
       not_2_out, not_3_out, not_4_out, not_5_out, not_6_out, not_7_out, not_8_out, not_9_out, not_10_out,
       not_11_out, not_12_out, not_13_out, not_14_out, not_15_out, not_16_out, or_1_out, or_2_out, or_3_out,
       xnor_1_out, xor_1_out;

  not not_1 (not_1_out, C);
  not not_2 (not_2_out, B);
  not not_3 (not_3_out, D);
  not not_4 (not_4_out, C);
  not not_5 (not_5_out, A);
  not not_6 (not_6_out, B);
  not not_7 (not_7_out, D);
  not not_8 (not_8_out, D);
  or or_1 (or_1_out, not_2_out, C);
  not not_9 (not_9_out, C);
  not not_10 (not_10_out, D);
  and and_1 (and_1_out, not_3_out, not_4_out);
  and and_2 (and_2_out, not_5_out, not_6_out, not_7_out);
  not not_11 (not_11_out, B);
  or or_2 (or_2_out, not_9_out, not_10_out);
  and and_3 (and_3_out, B, D);
  not not_12 (not_12_out, B);
  or or_3 (or_3_out, not_11_out, C);
  not not_13 (not_13_out, D);
  and and_4 (and_4_out, B, not_1_out, D);
  and and_5 (e, not_8_out, or_1_out);
  and and_6 (and_6_out, or_2_out, B);
  and and_7 (and_7_out, not_12_out, C);
  and and_8 (and_8_out, or_3_out, not_13_out);
  not not_14 (not_14_out, B);
  xnor xnor_1 (xnor_1_out, C, D);
  not not_15 (not_15_out, C);
  not not_16 (not_16_out, D);
  and and_9 (and_9_out, not_16_out, C);
  xor xor_1 (xor_1_out, C, B);
  or or_4 (a_2, A, C, and_3_out, and_2_out);
  or or_5 (b_2, not_14_out, xnor_1_out);
  or or_6 (c_2, A, B, not_15_out, D);
  or or_7 (d_2, A, and_7_out, and_8_out, and_4_out);
  or or_8 (f, A, and_6_out, and_1_out);
  or or_9 (g, A, and_9_out, xor_1_out);
endmodule

module ContadorBCDunidMIN (
  input  in_1,
  output Aunid,
  output Bunid,
  output Cunid,
  output Dunid,
  output TC
);

  wire and_1_out, and_2_out, clock_1_out, nand_1_out, nand_2_out, not_1_out, not_5_out;

  Clock clock_1 (.out(clock_1_out));
  J_K_Flip_Flop j_k_ff_1 (
    .J(1'b1), .clk(clock_1_out), .K(1'b1), .Q(Dunid), .en(in_1), .reset(not_1_out));  // open: Qn, preset
  not not_1 (not_1_out, nand_1_out);
  not not_2 (TC, nand_2_out);
  J_K_Flip_Flop j_k_ff_2 (
    .J(Dunid), .clk(clock_1_out), .K(Dunid), .Q(Cunid), .en(in_1), .reset(in_1));  // open: Qn, preset
  not not_3 (in_1, nand_1_out);
  nand nand_1 (nand_1_out, Cunid, Aunid);
  and and_1 (and_1_out, Dunid, Cunid);
  J_K_Flip_Flop j_k_ff_3 (
    .J(and_1_out), .clk(clock_1_out), .K(and_1_out), .Q(Bunid), .en(in_1), .reset(in_1));  // open: Qn, preset
  not not_4 (in_1, nand_1_out);
  and and_2 (and_2_out, Dunid, Cunid, Bunid);
  J_K_Flip_Flop j_k_ff_4 (
    .J(and_2_out), .clk(clock_1_out), .K(and_2_out), .Q(Aunid), .en(in_1), .reset(not_5_out));  // open: Qn, preset
  not not_5 (not_5_out, nand_1_out);
  nand nand_2 (nand_2_out, Aunid, Dunid, in_1);
endmodule

module ContadorBCDdezMIN (
  input  EN,
  output Adez,
  output Bdez,
  output Cdez,
  output Ddez,
  output out_6
);

  wire and_1_out, and_2_out, clock_1_out, nand_1_out, nand_2_out, not_1_out, not_3_out, not_4_out, not_5_out;

  Clock clock_1 (.out(clock_1_out));
  J_K_Flip_Flop j_k_ff_1 (
    .J(1'b1), .clk(clock_1_out), .K(1'b1), .Q(Ddez), .en(EN), .reset(not_1_out));  // open: Qn, preset
  not not_1 (not_1_out, nand_1_out);
  not not_2 (out_6, nand_2_out);
  J_K_Flip_Flop j_k_ff_2 (
    .J(Ddez), .clk(clock_1_out), .K(Ddez), .Q(Cdez), .en(EN), .reset(not_3_out));  // open: Qn, preset
  not not_3 (not_3_out, nand_1_out);
  nand nand_1 (nand_1_out, Cdez, Bdez);
  not not_4 (not_4_out, nand_1_out);
  and and_1 (and_1_out, Ddez, Cdez);
  J_K_Flip_Flop j_k_ff_3 (
    .J(and_1_out), .clk(clock_1_out), .K(and_1_out), .Q(Bdez), .en(EN), .reset(not_4_out));  // open: Qn, preset
  and and_2 (and_2_out, Ddez, Cdez, Bdez);
  J_K_Flip_Flop j_k_ff_4 (
    .J(and_2_out), .clk(clock_1_out), .K(and_2_out), .Q(Adez), .en(EN), .reset(not_5_out));  // open: Qn, preset
  not not_5 (not_5_out, nand_1_out);
  nand nand_2 (nand_2_out, Ddez, Bdez, EN);
endmodule

module ContadorBCDuniHORA (
  input  in_1,
  input  _2Hora,
  output Aunid,
  output Bunid,
  output Cunid,
  output Dunid,
  output TC,
  output meianoite
);

  wire and_1_out, and_2_out, clock_1_out, nand_1_out, nand_2_out, not_2_out, or_1_out;

  Clock clock_1 (.out(clock_1_out));
  J_K_Flip_Flop j_k_ff_1 (
    .J(1'b1), .clk(clock_1_out), .K(1'b1), .Q(Dunid), .en(in_1), .reset(or_1_out));  // open: Qn, preset
  not not_1 (TC, nand_2_out);
  J_K_Flip_Flop j_k_ff_2 (
    .J(Dunid), .clk(clock_1_out), .K(Dunid), .Q(Cunid), .en(in_1), .reset(or_1_out));  // open: Qn, preset
  nand nand_1 (nand_1_out, Cunid, Aunid);
  and and_1 (and_1_out, Dunid, Cunid);
  J_K_Flip_Flop j_k_ff_3 (
    .J(and_1_out), .clk(clock_1_out), .K(and_1_out), .Q(Bunid), .en(in_1), .reset(or_1_out));  // open: Qn, preset
  not not_2 (not_2_out, nand_1_out);
  and and_2 (and_2_out, Dunid, Cunid, Bunid);
  or or_1 (or_1_out, not_2_out, meianoite);
  J_K_Flip_Flop j_k_ff_4 (
    .J(and_2_out), .clk(clock_1_out), .K(and_2_out), .Q(Aunid), .en(in_1), .reset(or_1_out));  // open: Qn, preset
  nand nand_2 (nand_2_out, Aunid, Dunid, in_1);
  and and_3 (meianoite, Bunid, _2Hora);
endmodule

module ContadorBCDdezHORA (
  input  EN,
  input  meia_noite,
  output Adez,
  output Bdez,
  output Cdez,
  output Ddez,
  output _2hora
);

  wire and_1_out, and_2_out, clock_1_out, nand_1_out, not_1_out, or_1_out;

  Clock clock_1 (.out(clock_1_out));
  J_K_Flip_Flop j_k_ff_1 (
    .J(1'b1), .clk(clock_1_out), .K(1'b1), .Q(Ddez), .en(EN), .reset(or_1_out));  // open: Qn, preset
  J_K_Flip_Flop j_k_ff_2 (
    .J(Ddez), .clk(clock_1_out), .K(Ddez), .Q(_2hora), .en(EN), .reset(or_1_out));  // open: Qn, preset
  nand nand_1 (nand_1_out, _2hora, Ddez);
  and and_1 (and_1_out, Ddez, _2hora);
  J_K_Flip_Flop j_k_ff_3 (
    .J(and_1_out), .clk(clock_1_out), .K(and_1_out), .Q(Bdez), .en(EN), .reset(or_1_out));  // open: Qn, preset
  or or_1 (or_1_out, not_1_out, meia_noite);
  not not_1 (not_1_out, nand_1_out);
  and and_2 (and_2_out, Ddez, _2hora, Bdez);
  J_K_Flip_Flop j_k_ff_4 (
    .J(and_2_out), .clk(clock_1_out), .K(and_2_out), .Q(Adez), .en(EN), .reset(or_1_out));  // open: Qn, preset

  assign Cdez = _2hora;
endmodule

module teste (
  input  in_1
);

  wire contadorbcddezhora_1_p1, contadorbcddezhora_1_p2, contadorbcddezhora_1_p3, contadorbcddezhora_1_p4,
       contadorbcddezhora_1_p5, contadorbcdunihora_1_p3, contadorbcdunihora_1_p4, contadorbcdunihora_1_p5,
       contadorbcdunihora_1_p6, decoder_1_a_2, decoder_1_b_2, decoder_1_c_2, decoder_1_d_2, decoder_1_e,
       decoder_1_f, decoder_1_g, decoder_2_a_2, decoder_2_b_2, decoder_2_c_2, decoder_2_d_2, decoder_2_e,
       decoder_2_f, decoder_2_g;

  // ContadorBCDdezHORA contadorbcddezhora_1: pin names not known; wires that end beside it: contadorbcddezhora_1_p1, contadorbcddezhora_1_p2, contadorbcddezhora_1_p3, contadorbcddezhora_1_p4, contadorbcddezhora_1_p5
  Decoder decoder_1 (
    .A(contadorbcddezhora_1_p2), .B(contadorbcddezhora_1_p3), .C(contadorbcddezhora_1_p4),
    .D(contadorbcddezhora_1_p5), .a_2(decoder_1_a_2), .b_2(decoder_1_b_2), .c_2(decoder_1_c_2),
    .d_2(decoder_1_d_2), .e(decoder_1_e), .f(decoder_1_f), .g(decoder_1_g));
  _7_Segment_Display u_7_segment_display_1 (
    .g(decoder_1_g), .f(decoder_1_f), .a(decoder_1_a_2), .b(decoder_1_b_2), .e(decoder_1_e),
    .d(decoder_1_d_2), .c(decoder_1_c_2));  // open: dp
  _7_Segment_Display u_7_segment_display_2 (
    .g(decoder_2_g), .f(decoder_2_f), .a(decoder_2_a_2), .b(decoder_2_b_2), .e(decoder_2_e),
    .d(decoder_2_d_2), .c(decoder_2_c_2));  // open: dp
  // ContadorBCDuniHORA contadorbcdunihora_1: pin names not known; wires that end beside it: contadorbcddezhora_1_p1, in_1, contadorbcdunihora_1_p3, contadorbcdunihora_1_p4, contadorbcdunihora_1_p5, contadorbcdunihora_1_p6, contadorbcdunihora_1_p6
  Decoder decoder_2 (
    .A(contadorbcdunihora_1_p3), .B(contadorbcdunihora_1_p4), .C(contadorbcdunihora_1_p5),
    .D(contadorbcdunihora_1_p6), .a_2(decoder_2_a_2), .b_2(decoder_2_b_2), .c_2(decoder_2_c_2),
    .d_2(decoder_2_d_2), .e(decoder_2_e), .f(decoder_2_f), .g(decoder_2_g));
endmodule
