// Logisim project Sofia.circ as structural Verilog: 7 circuits, main circuit main
module main (
);

  wire contador01_1_a, decodera_1_a, decodera_1_b, decodera_1_c, decodera_1_d, decodera_1_e, decodera_1_f,
       decodera_1_g, decoderf_1_a, decoderf_1_b, decoderf_1_c, decoderf_1_d, decoderf_1_e, decoderf_1_f,
       decoderf_1_g, decoderi_1_a, decoderi_1_b, decoderi_1_c, decoderi_1_d, decoderi_1_e, decoderi_1_f,
       decoderi_1_g, decodero_1_a, decodero_1_b, decodero_1_c, decodero_1_d, decodero_1_e, decodero_1_f,
       decodero_1_g, decoders_1_a, decoders_1_b, decoders_1_c, decoders_1_d, decoders_1_e, decoders_1_f,
       decoders_1_g;

  Contador01 contador01_1 (.A(contador01_1_a));
  DecoderS decoders_1 (
    .in_1(contador01_1_a), .a(decoders_1_a), .b(decoders_1_b), .c(decoders_1_c), .d(decoders_1_d),
    .e(decoders_1_e), .f(decoders_1_f), .g(decoders_1_g));
  DecoderO decodero_1 (
    .in_1(contador01_1_a), .a(decodero_1_a), .b(decodero_1_b), .c(decodero_1_c), .d(decodero_1_d),
    .e(decodero_1_e), .f(decodero_1_f), .g(decodero_1_g));
  DecoderF decoderf_1 (
    .in_1(contador01_1_a), .a(decoderf_1_a), .b(decoderf_1_b), .c(decoderf_1_c), .d(decoderf_1_d),
    .e(decoderf_1_e), .f(decoderf_1_f), .g(decoderf_1_g));
  DecoderI decoderi_1 (
    .in_1(contador01_1_a), .a(decoderi_1_a), .b(decoderi_1_b), .c(decoderi_1_c), .d(decoderi_1_d),
    .e(decoderi_1_e), .f(decoderi_1_f), .g(decoderi_1_g));
  DecoderA decodera_1 (
    .in_1(contador01_1_a), .a(decodera_1_a), .b(decodera_1_b), .c(decodera_1_c), .d(decodera_1_d),
    .e(decodera_1_e), .f(decodera_1_f), .g(decodera_1_g));
  _7_Segment_Display u_7_segment_display_1 (
    .g(decoders_1_g), .f(decoders_1_f), .a(decoders_1_a), .b(decoders_1_b), .e(decoders_1_e),
    .d(decoders_1_d), .c(decoders_1_c));  // open: dp
  _7_Segment_Display u_7_segment_display_2 (
    .g(decodero_1_g), .f(decodero_1_f), .a(decodero_1_a), .b(decodero_1_b), .e(decodero_1_e),
    .d(decodero_1_d), .c(decodero_1_c));  // open: dp
  _7_Segment_Display u_7_segment_display_3 (
    .g(decoderf_1_g), .f(decoderf_1_f), .a(decoderf_1_a), .b(decoderf_1_b), .e(decoderf_1_e),
    .d(decoderf_1_d), .c(decoderf_1_c));  // open: dp
  _7_Segment_Display u_7_segment_display_4 (
    .g(decoderi_1_g), .f(decoderi_1_f), .a(decoderi_1_a), .b(decoderi_1_b), .e(decoderi_1_e),
    .d(decoderi_1_d), .c(decoderi_1_c));  // open: dp
  _7_Segment_Display u_7_segment_display_5 (
    .g(decodera_1_g), .f(decodera_1_f), .a(decodera_1_a), .b(decodera_1_b), .e(decodera_1_e),
    .d(decodera_1_d), .c(decodera_1_c));  // open: dp
endmodule

module Contador01 (
  output A
);

  wire clock_1_out;

  Clock clock_1 (.out(clock_1_out));
  J_K_Flip_Flop j_k_ff_1 (.J(1'b1), .clk(clock_1_out), .K(1'b1), .Q(A));  // open: Qn, preset, en, reset
endmodule

module DecoderS (
  input  in_1,
  output a,
  output b,
  output c,
  output d,
  output e,
  output f,
  output g
);


  assign a = in_1;
  assign b = 1'b0;
  assign c = in_1;
  assign d = in_1;
  assign e = 1'b0;
  assign f = in_1;
  assign g = in_1;
endmodule

module DecoderO (
  input  in_1,
  output a,
  output b,
  output c,
  output d,
  output e,
  output f,
  output g
);


  assign a = in_1;
  assign b = in_1;
  assign c = in_1;
  assign d = in_1;
  assign e = in_1;
  assign f = in_1;
  assign g = 1'b0;
endmodule

module DecoderF (
  input  in_1,
  output a,
  output b,
  output c,
  output d,
  output e,
  output f,
  output g
);


  assign a = in_1;
  assign b = 1'b0;
  assign c = 1'b0;
  assign d = 1'b0;
  assign e = in_1;
  assign f = in_1;
  assign g = in_1;
endmodule

module DecoderI (
  input  in_1,
  output a,
  output b,
  output c,
  output d,
  output e,
  output f,
  output g
);


  assign a = 1'b0;
  assign b = in_1;
  assign c = in_1;
  assign d = 1'b0;
  assign e = 1'b0;
  assign f = 1'b0;
  assign g = 1'b0;
endmodule

module DecoderA (
  input  in_1,
  output a,
  output b,
  output c,
  output d,
  output e,
  output f,
  output g
);


  assign a = in_1;
  assign b = in_1;
  assign c = in_1;
  assign d = 1'b0;
  assign e = in_1;
  assign f = in_1;
  assign g = in_1;
endmodule
